# Fritzing sketch Agrivoltaics (saved by Fritzing 0.9.3b)
breadboards: 1
perfboards: 1

parts:
  M1 = ESP32-S3-DevKitC-1-N8R8-v1 [part_number=ESP32-S3-DevKitC-1-N8R8-v1]
  U1 = 4-Channel 5v Relay Shield [package=relay-4ch5v10a]  # not connected
  M2 = MAX485 Breakout [package=THT]
  TSYS1 = TSYS01 [package="SIP (Single Inline) [THT]"]  # not connected
  U2 = LM2596 step down module  # not connected

nets:
  N1: M1.pin_1, M1.pin_2
  N2: M1.pin_22, M1.pin_23, M1.pin_24, M1.pin_44
  N3: M2.A, M2.A1

custom parts:
  ESP32-S3-DevKitC-1-N8R8-v1: ESP32-S3-DevKitC-1-N8R8-v1 This module is 44pins long (2x22) and 11 pins width.
  4-Channel 5v Relay Shield: 4 Channel 5v Relay Shield w. 2x SPD-06VDC-SD-C
  MAX485 Breakout: MAX485 RS485 breakout board
  TSYS01: Temperature sensor I2C 0.1 degrees accurate
  LM2596 step down module: LM2596 DC-DC step down power supply module 3 A.
